# Fritzing sketch ArduinoSetupSketch (saved by Fritzing 0.9.3b)
breadboards: 1

parts:
  Bauteil1 = Arduino Due (Rev2b)
  R1 = Resistor [tolerance=±5% resistance=220 package="0603 [SMD]"]
  J1 = Basic Force Sensing Resistor (FSR) [package=THT]
  Bauteil2 = 9 Degrees of Freedom - Sensor Stick
  Bauteil3 = Bluetooth HC-05 Macho

nets:
  N1: Bauteil1.A0, R1.Pin_1, J1.pin_0
  N2: Bauteil1.D14/TX3, Bauteil3.RXD
  N3: Bauteil1.D15/RX3, Bauteil3.TXD
  N4: Bauteil1.D16/TX2, Bauteil2.SCL
  N5: Bauteil1.D17/RX2, Bauteil2.SDA
  VCC: Bauteil1.IOREF, J1.pin_1, Bauteil2.VCC, Bauteil3.VCC
  GND: Bauteil1.GND, R1.Pin_0, Bauteil2.GND, Bauteil3.GND
